# Fritzing sketch maket (saved by Fritzing 0.9.2b)
circuit board: 8.46667cm x 5.64444cm
breadboards: 2

parts:
  DTH11 = Humidity and Temperature Sensor RHT03
  R2 = Resistor [tolerance=±5% resistance=10k package=THT]
  R6 = Resistor [tolerance=±5% resistance=3.3k package=THT]
  R7 = Resistor [tolerance=±5% resistance=3.3k package=THT]
  Деталь2 = Arduino Mini (Rev5)
  resistors = Resistor [tolerance=±5% resistance=3.3k package=THT]
  R11 = Photocell (LDR) [package=THT]
  resistors_2 = Resistor [tolerance=±5% resistance=3.3k package=THT]
  R13 = Resistor [tolerance=±5% resistance=10k package=THT]
  R14 = Resistor [tolerance=±5% resistance=10k package=THT]
  R15 = Resistor [tolerance=±5% resistance=10k package=THT]
  R16 = Resistor [tolerance=±5% resistance=150 package=THT]
  BPM180 = Barometric Pressure Sensor - BMP085 Breakout
  U1 = Graphical LCD 128x64 [package=lcd-g12864]
  R17 = Resistor [tolerance=±5% resistance=1.8k package=THT]
  R18 = Resistor [tolerance=±5% resistance=1.8k package=THT]
  R19 = Resistor [tolerance=±5% resistance=1.8k package=THT]
  R20 = Resistor [tolerance=±5% resistance=1.8k package=THT]
  R21 = Resistor [tolerance=±5% resistance=1.8k package=THT]
  R22 = Resistor [tolerance=±5% resistance=3.3k package=THT]
  resistors1 = Resistor [tolerance=±5% resistance=3.3k package=THT]
  Деталь3 = Real Time Clock Module - DS1307 RTC Breakout Board
  Q1 = PHOTOTRANSISTOR REFLECTIVE OBJECT SENSOR [package=qrb1114-side]
  R23 = Resistor [tolerance=±5% resistance=510 package=THT]
  R24 = Resistor [tolerance=±5% resistance=10k package=THT]

nets:
  N1: DTH11.Vcc, R2.Pin_1
  5V: DTH11.Data-signal, R2.Pin_0, Деталь2.D9_PWM, Деталь2.5V, R11.pin_0, R14.Pin_1, R15.Pin_1, BPM180.VCC, U1.DB4, Деталь3.5V, Q1.A, Q1.E
  GND: DTH11.GND_2, R6.Pin_1, R7.Pin_1, Деталь2.GND, resistors.Pin_1, resistors_2.Pin_1, R13.Pin_0, BPM180.GND, U1.DB3, R22.Pin_1, resistors1.Pin_1, Деталь3.GND, R23.Pin_0, R24.Pin_0
  N2: R6.Pin_0, U1.VSS, R21.Pin_0
  N3: R7.Pin_0, U1.DB1, R18.Pin_0
  N4: Деталь2.D2, R17.Pin_1
  N5: Деталь2.D3_PWM, R18.Pin_1
  N6: Деталь2.D4, R19.Pin_1
  N7: Деталь2.D5_PWM, R20.Pin_1
  N8: Деталь2.D6_PWM, R21.Pin_1
  N9: Деталь2.D7, R16.Pin_1
  N10: Деталь2.A6, R11.pin_1, R13.Pin_1
  N11: Деталь2.A4, R14.Pin_0, BPM180.SDA
  N12: Деталь2.A7, Q1.C, R24.Pin_1
  N13: Деталь2.A5, R15.Pin_0, BPM180.SCL, Деталь3.SCL, Деталь3.SDA
  N14: resistors.Pin_0, U1.DB0, R19.Pin_0, resistors1.Pin_0
  N15: resistors_2.Pin_0, U1.DB2, R17.Pin_0
  N16: R16.Pin_0, U1.VDD
  N17: U1.VO, R20.Pin_0, R22.Pin_0
  N18: Q1.K, R23.Pin_1

notes:
  SDA
  SCL
  VCC
  GND
  BMP180
  ARDUINO MINI PRO
  LED
  SCE
  RST
  D/C
  DN<MOSI>
  SCLK
  5110 lcd display
  TCRT5000
  ds1307
